// Logisim project 4bit_sort.circ as structural Verilog
module _1bit_swap (
  input  A,
  input  B,
  input  Judge,
  output A1,
  output B1
);

  wire and_1_out, and_2_out, and_3_out, and_4_out, not_1_out, not_2_out;

  not not_1 (not_1_out, Judge);
  not not_2 (not_2_out, Judge);
  and and_1 (and_1_out, B, Judge);
  and and_2 (and_2_out, A, not_1_out);
  and and_3 (and_3_out, B, not_2_out);
  and and_4 (and_4_out, A, Judge);
  or or_1 (A1, and_1_out, and_2_out);
  or or_2 (B1, and_3_out, and_4_out);
endmodule

module _4bit_swap (
  input  [3:0] A,
  input  [3:0] B,
  input  J,
  output [3:0] X,
  output [3:0] Y
);

  _1bit_swap u_1bit_swap_1 (.A(A[3]), .B(B[3]), .Judge(J), .A1(X[3]), .B1(Y[3]));
  _1bit_swap u_1bit_swap_2 (.A(A[2]), .B(B[2]), .Judge(J), .A1(X[2]), .B1(Y[2]));
  _1bit_swap u_1bit_swap_3 (.A(A[1]), .B(B[1]), .Judge(J), .A1(X[1]), .B1(Y[1]));
  _1bit_swap u_1bit_swap_4 (.A(A[0]), .B(B[0]), .Judge(J), .A1(X[0]), .B1(Y[0]));

  // Other names for the same wires on the sheet: Judge = J
endmodule
