// Logisim project ALU.circ as structural Verilog: 1 circuit, main circuit alu
module alu (
  input  [3:0] A,
  input  [3:0] B,
  input  [1:0] ALUop,
  output [3:0] C
);

  wire [3:0] adder_1_out, and_1_out, or_1_out, subtractor_1_out;

  assign and_1_out = A & B;  // AND_Gate and_1, 4 bits wide
  assign or_1_out = A | B;  // OR_Gate or_1, 4 bits wide
  Adder #(.width(4)) adder_1 (.a(A), .b(B), .out(adder_1_out));  // open: cin, cout
  Subtractor #(.width(4)) subtractor_1 (.a(A), .b(B), .out(subtractor_1_out));  // open: bin, bout
  Multiplexer #(.select(2), .width(4), .enable("false")) multiplexer_1 (
    .in0(adder_1_out), .in1(subtractor_1_out), .in2(and_1_out), .in3(or_1_out), .out(C), .sel(ALUop));
endmodule
