// Logisim project CRC_8.circ as structural Verilog: 3 circuits, main circuit CRC
module CRC (
  input  [7:0] A,
  input  [3:0] B,
  output [10:0] C
);

  wire and_1_out, and_2_out, and_3_out, and_4_out, and_5_out, and_6_out, and_7_out, and_8_out, and_9_out,
       and_10_out, and_11_out, and_12_out, and_13_out, and_14_out, and_15_out, and_16_out, and_17_out,
       and_18_out, and_19_out, and_20_out, and_21_out, and_22_out, and_23_out, and_24_out, and_25_out,
       and_26_out, and_27_out, and_28_out, and_29_out, and_30_out, and_31_out, and_32_out, and_33_out,
       and_34_out, and_35_out, and_36_out, and_37_out, and_38_out, and_39_out, and_40_out, and_41_out,
       and_42_out, and_43_out, and_44_out, and_45_out, and_46_out, and_47_out, and_48_out, not_1_out,
       not_2_out, not_3_out, not_4_out, not_5_out, not_6_out, not_7_out, not_8_out, or_1_out, or_2_out,
       or_3_out, or_4_out, or_5_out, or_6_out, or_7_out, or_8_out, or_9_out, or_10_out, or_11_out, or_12_out,
       or_13_out, or_14_out, or_15_out, or_16_out, or_17_out, or_18_out, or_19_out, or_20_out, or_21_out,
       xor_1_out, xor_2_out, xor_3_out, xor_4_out, xor_5_out, xor_6_out, xor_7_out, xor_8_out, xor_9_out,
       xor_10_out, xor_11_out, xor_12_out, xor_13_out, xor_14_out, xor_15_out, xor_16_out, xor_17_out,
       xor_18_out, xor_19_out, xor_20_out, xor_21_out, xor_22_out, xor_23_out, xor_24_out;

  not not_1 (not_1_out, A[7]);
  xor xor_1 (xor_1_out, A[6], B[2]);
  xor xor_2 (xor_2_out, A[5], B[1]);
  xor xor_3 (xor_3_out, A[4], B[0]);
  xor xor_4 (xor_4_out, or_14_out, B[2]);
  xor xor_5 (xor_5_out, or_15_out, B[1]);
  xor xor_6 (xor_6_out, A[1], B[0]);
  and and_1 (and_1_out, A[7], xor_1_out);
  and and_2 (and_2_out, A[7], xor_2_out);
  and and_3 (and_3_out, A[7], xor_3_out);
  not not_2 (not_2_out, or_13_out);
  and and_4 (and_4_out, or_13_out, xor_4_out);
  and and_5 (and_5_out, or_13_out, xor_5_out);
  and and_6 (and_6_out, or_13_out, xor_6_out);
  and and_7 (and_7_out, not_1_out, A[6]);
  and and_8 (and_8_out, not_1_out, A[5]);
  and and_9 (and_9_out, not_1_out, A[4]);
  or or_1 (or_1_out, and_7_out, and_1_out);
  or or_2 (or_2_out, and_2_out, and_8_out);
  or or_3 (or_3_out, and_3_out, and_9_out);
  and and_10 (and_10_out, not_2_out, or_14_out);
  and and_11 (and_11_out, not_2_out, or_15_out);
  and and_12 (and_12_out, not_2_out, A[1]);
  or or_4 (or_4_out, and_10_out, and_4_out);
  or or_5 (or_5_out, and_5_out, and_11_out);
  or or_6 (or_6_out, and_6_out, and_12_out);
  xor xor_7 (xor_7_out, or_2_out, B[2]);
  xor xor_8 (xor_8_out, or_3_out, B[1]);
  xor xor_9 (xor_9_out, A[3], B[0]);
  not not_3 (not_3_out, or_1_out);
  and and_13 (and_13_out, or_1_out, xor_7_out);
  and and_14 (and_14_out, or_1_out, xor_8_out);
  and and_15 (and_15_out, or_1_out, xor_9_out);
  xor xor_10 (xor_10_out, or_5_out, B[2]);
  xor xor_11 (xor_11_out, or_6_out, B[1]);
  xor xor_12 (xor_12_out, A[0], B[0]);
  and and_16 (and_16_out, not_3_out, or_2_out);
  and and_17 (and_17_out, not_3_out, or_3_out);
  and and_18 (and_18_out, not_3_out, A[3]);
  or or_7 (or_7_out, and_16_out, and_13_out);
  or or_8 (or_8_out, and_14_out, and_17_out);
  or or_9 (or_9_out, and_15_out, and_18_out);
  not not_4 (not_4_out, or_4_out);
  and and_19 (and_19_out, or_4_out, xor_10_out);
  and and_20 (and_20_out, or_4_out, xor_11_out);
  and and_21 (and_21_out, or_4_out, xor_12_out);
  xor xor_13 (xor_13_out, or_8_out, B[2]);
  xor xor_14 (xor_14_out, or_9_out, B[1]);
  xor xor_15 (xor_15_out, A[2], B[0]);
  and and_22 (and_22_out, not_4_out, or_5_out);
  or or_10 (or_10_out, and_22_out, and_19_out);
  or or_11 (or_11_out, and_20_out, and_23_out);
  and and_23 (and_23_out, not_4_out, or_6_out);
  or or_12 (or_12_out, and_21_out, and_24_out);
  and and_24 (and_24_out, not_4_out, A[0]);
  not not_5 (not_5_out, or_7_out);
  and and_25 (and_25_out, or_7_out, xor_13_out);
  and and_26 (and_26_out, or_7_out, xor_14_out);
  and and_27 (and_27_out, or_7_out, xor_15_out);
  xor xor_16 (xor_16_out, or_11_out, B[2]);
  xor xor_17 (xor_17_out, or_12_out, B[1]);
  xor xor_18 (xor_18_out, 1'b0, B[0]);
  and and_28 (and_28_out, not_5_out, or_8_out);
  and and_29 (and_29_out, not_5_out, or_9_out);
  and and_30 (and_30_out, not_5_out, A[2]);
  not not_6 (not_6_out, or_10_out);
  or or_13 (or_13_out, and_28_out, and_25_out);
  or or_14 (or_14_out, and_26_out, and_29_out);
  or or_15 (or_15_out, and_27_out, and_30_out);
  and and_31 (and_31_out, or_10_out, xor_16_out);
  and and_32 (and_32_out, or_10_out, xor_17_out);
  and and_33 (and_33_out, or_10_out, xor_18_out);
  and and_34 (and_34_out, not_6_out, or_11_out);
  and and_35 (and_35_out, not_6_out, or_12_out);
  and and_36 (and_36_out, not_6_out, 1'b0);
  or or_16 (or_16_out, and_34_out, and_31_out);
  or or_17 (or_17_out, and_32_out, and_35_out);
  or or_18 (or_18_out, and_33_out, and_36_out);
  xor xor_19 (xor_19_out, or_17_out, B[2]);
  xor xor_20 (xor_20_out, or_18_out, B[1]);
  xor xor_21 (xor_21_out, 1'b0, B[0]);
  not not_7 (not_7_out, or_16_out);
  and and_37 (and_37_out, or_16_out, xor_19_out);
  and and_38 (and_38_out, or_16_out, xor_20_out);
  and and_39 (and_39_out, or_16_out, xor_21_out);
  and and_40 (and_40_out, not_7_out, or_17_out);
  and and_41 (and_41_out, not_7_out, or_18_out);
  and and_42 (and_42_out, not_7_out, 1'b0);
  or or_19 (or_19_out, and_40_out, and_37_out);
  or or_20 (or_20_out, and_38_out, and_41_out);
  or or_21 (or_21_out, and_39_out, and_42_out);
  xor xor_22 (xor_22_out, or_20_out, B[2]);
  xor xor_23 (xor_23_out, or_21_out, B[1]);
  xor xor_24 (xor_24_out, 1'b0, B[0]);
  not not_8 (not_8_out, or_19_out);
  and and_43 (and_43_out, or_19_out, xor_22_out);
  and and_44 (and_44_out, or_19_out, xor_23_out);
  and and_45 (and_45_out, or_19_out, xor_24_out);
  and and_46 (and_46_out, not_8_out, or_20_out);
  and and_47 (and_47_out, not_8_out, or_21_out);
  and and_48 (and_48_out, not_8_out, 1'b0);
  or or_22 (C[2], and_46_out, and_43_out);
  or or_23 (C[1], and_44_out, and_47_out);
  or or_24 (C[0], and_45_out, and_48_out);

  assign C[10:3] = A;

  // Other names for the same wires on the sheet: z = B[0]; y = B[1]; x = B[2]; _0 = C[0]; _1 = C[1]; _2 = C[2];
  //   _3 = A[0]; _4 = A[1]; _5 = A[2]; _6 = A[3]; _7 = A[4]; _8 = A[5]; _9 = A[6]; _10 = A[7]
endmodule

module XOR_4 (
  input  [3:0] in_1,
  input  [3:0] in_2,
  output [2:0] out_3
);

  wire and_1_out, and_2_out, and_3_out, and_4_out, and_5_out, and_6_out, not_1_out, xor_1_out, xor_2_out,
       xor_3_out;

  xor xor_1 (xor_1_out, in_1[2], in_2[2]);
  xor xor_2 (xor_2_out, in_1[1], in_2[1]);
  xor xor_3 (xor_3_out, in_1[0], in_2[0]);
  not not_1 (not_1_out, in_1[3]);
  and and_1 (and_1_out, in_1[3], xor_1_out);
  and and_2 (and_2_out, in_1[3], xor_2_out);
  and and_3 (and_3_out, in_1[3], xor_3_out);
  and and_4 (and_4_out, not_1_out, in_1[2]);
  and and_5 (and_5_out, not_1_out, in_1[1]);
  and and_6 (and_6_out, not_1_out, in_1[0]);
  or or_1 (out_3[2], and_4_out, and_1_out);
  or or_2 (out_3[1], and_2_out, and_5_out);
  or or_3 (out_3[0], and_3_out, and_6_out);
endmodule

module XOR (
);

  wire and_1_out, and_2_out, and_3_out, and_4_out, and_5_out, and_6_out, not_1_out, or_1_out, or_2_out,
       or_3_out, undriven, undriven_2, undriven_3, undriven_4, undriven_5, undriven_6, undriven_7, xor_1_out,
       xor_2_out, xor_3_out;

  xor xor_1 (xor_1_out, undriven_2, undriven_5);
  xor xor_2 (xor_2_out, undriven_3, undriven_6);
  xor xor_3 (xor_3_out, undriven_4, undriven_7);
  not not_1 (not_1_out, undriven);
  and and_1 (and_1_out, undriven, xor_1_out);
  and and_2 (and_2_out, undriven, xor_2_out);
  and and_3 (and_3_out, undriven, xor_3_out);
  and and_4 (and_4_out, not_1_out, undriven_2);
  and and_5 (and_5_out, not_1_out, undriven_3);
  and and_6 (and_6_out, not_1_out, undriven_4);
  or or_1 (or_1_out, and_4_out, and_1_out);
  or or_2 (or_2_out, and_2_out, and_5_out);
  or or_3 (or_3_out, and_3_out, and_6_out);
endmodule
