// Logisim project FSM.circ as structural Verilog
module fsm (
  input  CLR,
  input  [1:0] In,
  output Z
);

  wire CLK_out, d_ff_1_q, ni0, ni1, not_1_out, nr0, nr1, r0, r0i, r1, r1i;

  D_Flip_Flop d_ff_1 (.clk(CLK_out), .D(CLR), .Q(d_ff_1_q), .reset(not_1_out));  // open: Qn, preset, en
  not not_1 (not_1_out, CLR);
  not not_2 (ni1, In[1]);
  not not_3 (ni0, In[0]);
  Clock CLK (.out(CLK_out));
  and and_1 (r0i, ni1, In[0]);
  Register #(.width(1)) u_R0 (.D(r0i), .Q(r0), .clk(CLK_out), .clr(d_ff_1_q));  // open: en
  not not_4 (nr0, r0);
  Register #(.width(1)) u_R1 (.D(r1i), .Q(r1), .clk(CLK_out), .clr(d_ff_1_q));  // open: en
  and and_2 (r1i, nr1, r0, ni0);
  not not_5 (nr1, r1);
  and and_3 (Z, nr0, ni0, r1);

  // Other names for the same wires on the sheet: i0 = In[0]; i1 = In[1]
endmodule
