// Logisim project P0-fsm.circ as structural Verilog: 2 circuits, main circuit fsm
module std (
  input  i1,
  input  i0,
  output a,
  output b,
  output c,
  output e
);

  wire not_1_out, not_2_out, not_3_out, not_4_out;

  not not_1 (not_1_out, i1);
  not not_2 (not_2_out, i0);
  not not_3 (not_3_out, i1);
  not not_4 (not_4_out, i0);
  and and_1 (e, i1, i0);
  and and_2 (a, not_1_out, not_2_out);
  and and_3 (b, not_3_out, i0);
  and and_4 (c, i1, not_4_out);
endmodule

module fsm (
  input  [1:0] in,
  input  clr,
  output out
);

  wire _1, _2, a, and_1_out, and_2_out, and_3_out, and_4_out, b, c, clk, e, na, nb, nc, ne, nr0, nr1, nr2,
       r0, r1, r2;

  not not_1 (na, a);
  std std_1 (.i1(in[1]), .i0(in[0]), .a(a), .b(b), .c(c), .e(e));
  not not_2 (ne, e);
  not not_3 (nb, b);
  not not_4 (nc, c);
  Clock u_clk (.out(clk));
  and and_1 (and_1_out, nr2, r1, nr0, b);
  and and_2 (and_2_out, nr2, r1, nr0, c);
  Register #(.width(1)) register_1 (.D(b), .Q(r0), .clk(clk), .clr(clr));  // open: en
  Register #(.width(1)) register_2 (.D(_1), .Q(r1), .clk(clk), .clr(clr));  // open: en
  Register #(.width(1)) register_3 (.D(_2), .Q(r2), .clk(clk), .clr(clr));  // open: en
  or or_1 (out, and_1_out, and_2_out);
  not not_5 (nr0, r0);
  not not_6 (nr1, r1);
  not not_7 (nr2, r2);
  and and_3 (and_3_out, nr2, nr1, r0, a);
  and and_4 (and_4_out, r2, nr1, nr0, a);
  and and_5 (_2, nr2, r1, nr0, c);
  or or_2 (_1, and_3_out, and_4_out);
endmodule
