// Logisim project CPU_withmore.circ as structural Verilog: 6 circuits, main circuit main
module main (
  input  reset,
  output [31:0] out_2,
  output out_3,
  output [4:0] out_4,
  output [31:0] out_5,
  output out_6,
  output [4:0] out_7,
  output [31:0] out_8
);

  wire ALUSrc, Branch, clk, isJ, isLHU, MemtoReg, RegDst;
  wire [1:0] EXTop;
  wire [2:0] ALUop;
  wire [4:0] multiplexer_3_out;
  wire [15:0] multiplexer_5_out;
  wire [31:0] A, B, Data, imm32, multiplexer_2_out, multiplexer_4_out, PC_4, ram_1_data, Result_ALU;

  Clock u_clk (.out(clk));
  IFU ifu_1 (
    .CLK(clk), .Reset(reset), .Branch(Branch), .Zero({Result_ALU[31:7], out_7, Result_ALU[1:0]}), .isJ(isJ),
    .Instr(out_2), .PC_4(PC_4));
  EXT ext_1 (.imm16(out_2[15:0]), .EXTop(EXTop), .Result_EXT(imm32));
  Controller controller_1 (
    .opcode(out_2[31:26]), .funct(out_2[5:0]), .MemtoReg(MemtoReg), .MemWrite(out_6), .Branch(Branch),
    .ALUSrc(ALUSrc), .RegDst(RegDst), .RegWrite(out_3), .EXTop(EXTop), .ALUop(ALUop), .isJ(isJ), .isLHU(isLHU));
  Multiplexer #(.width(5)) multiplexer_1 (
    .in0(out_2[20:16]), .in1(out_2[15:11]), .out(out_4), .sel(RegDst));  // open: en
  Multiplexer #(.width(32)) multiplexer_2 (.in0(out_5), .in1(PC_4), .out(multiplexer_2_out), .sel(isJ));  // open: en
  Multiplexer #(.width(5)) multiplexer_3 (.in0(out_4), .in1(5'b11110), .out(multiplexer_3_out), .sel(isJ));  // open: en
  Multiplexer #(.width(32)) multiplexer_4 (
    .in0(multiplexer_2_out), .in1(Data), .out(multiplexer_4_out), .sel(isLHU));  // open: en
  GRF grf_1 (
    .A1(out_2[25:21]), .A2(out_2[20:16]), .A3(multiplexer_3_out), .WD(multiplexer_4_out), .clk(clk),
    .reset(reset), .WE3(out_3), .RD1(A), .RD2(out_8));
  Multiplexer #(.width(16)) multiplexer_5 (
    .in0(out_5[15:0]), .in1(out_5[31:16]), .out(multiplexer_5_out), .sel(out_7[1]));  // open: en
  Multiplexer #(.width(32)) multiplexer_6 (.in0(out_8), .in1(imm32), .out(B), .sel(ALUSrc));  // open: en
  assign Data = {{16{1'b0}}, multiplexer_5_out};  // Bit_Extender bit_extender_1
  ALU alu_1 (.A(A), .B(B), .ALUop(ALUop), .Result_ALU({Result_ALU[31:7], out_7, Result_ALU[1:0]}));
  RAM #(.addrWidth(5), .dataWidth(32), .bus("separate")) ram_1 (
    .addr(out_7), .din(out_8), .data(ram_1_data), .str(out_6), .clk(clk));  // open: sel, ld, clr
  Multiplexer #(.width(32)) multiplexer_7 (
    .in0({Result_ALU[31:7], out_7, Result_ALU[1:0]}), .in1(ram_1_data), .out(out_5), .sel(MemtoReg));  // open: en

  // Other names for the same wires on the sheet: funct[5:0] = out_2[5:0]; imm16[15:0] = out_2[15:0];
  //   Instr[31:0] = out_2; rt[4:0] = out_2[20:16]; GRF_B[31:0] = out_8; MemData[31:0] = out_8; MemWrite = out_6;
  //   opcode[5:0] = out_2[31:26]; rd[4:0] = out_2[15:11]; RegAddr[4:0] = out_4; RegWrite = out_3;
  //   MemAddr[4:0] = out_7; Result_ALU[6:2] = out_7; byte = out_7[1]; rs[4:0] = out_2[25:21]; RegData[31:0] = out_5;
  //   WD[31:0] = out_5; WD_0_15[15:0] = out_5[15:0]; WD_16_31[15:0] = out_5[31:16]
endmodule

module ALU (
  input  [31:0] A,
  input  [31:0] B,
  input  [2:0] ALUop,
  output [31:0] Result_ALU
);

  wire [31:0] Result_Addu, Result_Andi, Result_Ori, Result_Subu;

  Adder #(.width(32)) adder_1 (.a(A), .b(B), .out(Result_Addu));  // open: cin, cout
  Subtractor #(.width(32)) subtractor_1 (.a(A), .b(B), .out(Result_Subu));  // open: bin, bout
  assign Result_Ori = A | B;  // OR_Gate or_1, 32 bits wide
  assign Result_Andi = A & B;  // AND_Gate and_1, 32 bits wide
  Multiplexer #(.select(3), .width(32)) multiplexer_1 (
    .in0(Result_Addu), .in1(Result_Subu), .in2(Result_Ori), .in3(Result_Andi), .out(Result_ALU), .sel(ALUop));  // open: in4, in5, in6, in7, en
endmodule

module EXT (
  input  [15:0] imm16,
  input  [1:0] EXTop,
  output [31:0] Result_EXT
);

  wire [31:0] bit_extender_1_out, bit_extender_2_out;

  assign bit_extender_1_out = {{16{1'b0}}, imm16};  // Bit_Extender bit_extender_1
  assign bit_extender_2_out = {{16{imm16[15]}}, imm16};  // Bit_Extender bit_extender_2
  Multiplexer #(.select(2), .width(32)) multiplexer_1 (
    .in0(bit_extender_1_out), .in1(bit_extender_2_out), .in2({imm16, {16{1'b0}}}), .out(Result_EXT),
    .sel(EXTop));  // open: in3, en
endmodule

module GRF (
  input  clk,
  input  reset,
  input  WE3,
  input  [4:0] A1,
  input  [4:0] A2,
  input  [4:0] A3,
  input  [31:0] WD,
  output [31:0] RD1,
  output [31:0] RD2
);

  wire undriven;
  wire [31:0] i1, i2, i3, i4, i5, i6, i7, i8, i9, i10, i11, i12, i13, i14, i15, i16, i17, i18, i19, i20, i21,
       i22, i23, i24, i25, i26, i27, i28, i29, i30, i31, o0, o1, o2, o3, o4, o5, o6, o7, o8, o9, o10, o11,
       o12, o13, o14, o15, o16, o17, o18, o19, o20, o21, o22, o23, o24, o25, o26, o27, o28, o29, o30, o31;

  Demultiplexer #(.select(5), .width(32), .tristate("true")) demultiplexer_1 (
    .out1(i1), .out2(i2), .out3(i3), .out4(i4), .out5(i5), .out6(i6), .out7(i7), .out8(i8), .out9(i9),
    .out10(i10), .out11(i11), .out12(i12), .out13(i13), .out14(i14), .out15(i15), .out16(i16), .out17(i17),
    .out18(i18), .out19(i19), .out20(i20), .out21(i21), .out22(i22), .out23(i23), .out24(i24), .out25(i25),
    .out26(i26), .out27(i27), .out28(i28), .out29(i29), .out30(i30), .out31(i31), .in(WD), .sel(A3), .en(WE3));  // open: out0
  Register #(.width(32)) _0 (.D({32{1'b0}}), .Q(o0), .clk(clk), .clr(reset));  // open: en
  Register #(.width(32)) _1 (.D(i1), .Q(o1), .clk(clk), .clr(reset));  // open: en
  Register #(.width(32)) _2 (.D(i2), .Q(o2), .clk(clk), .clr(reset));  // open: en
  Register #(.width(32)) register_1 (.D(i3), .Q(o3), .clk(clk), .clr(reset));  // open: en
  Register #(.width(32)) _4 (.D(i4), .Q(o4), .clk(clk), .clr(reset));  // open: en
  Register #(.width(32)) _5 (.D(i5), .Q(o5), .clk(clk), .clr(reset));  // open: en
  Register #(.width(32)) _6 (.D(i6), .Q(o6), .clk(clk), .clr(reset));  // open: en
  Register #(.width(32)) _7 (.D(i7), .Q(o7), .clk(clk), .clr(reset));  // open: en
  Register #(.width(32)) _8 (.D(i8), .Q(o8), .clk(clk), .clr(reset));  // open: en
  Register #(.width(32)) _9 (.D(i9), .Q(o9), .clk(clk), .clr(reset));  // open: en
  Register #(.width(32)) _10 (.D(i10), .Q(o10), .clk(clk), .clr(reset));  // open: en
  Register #(.width(32)) _11 (.D(i11), .Q(o11), .clk(clk), .clr(reset));  // open: en
  Register #(.width(32)) _12 (.D(i12), .Q(o12), .clk(clk), .clr(reset));  // open: en
  Register #(.width(32)) _13 (.D(i13), .Q(o13), .clk(clk), .clr(reset));  // open: en
  Register #(.width(32)) _14 (.D(i14), .Q(o14), .clk(clk), .clr(reset));  // open: en
  Register #(.width(32)) _15 (.D(i15), .Q(o15), .clk(clk), .clr(reset));  // open: en
  Register #(.width(32)) _16 (.D(i16), .Q(o16), .clk(clk), .clr(reset));  // open: en
  Register #(.width(32)) _17 (.D(i17), .Q(o17), .clk(clk), .clr(reset));  // open: en
  Register #(.width(32)) _18 (.D(i18), .Q(o18), .clk(clk), .clr(reset));  // open: en
  Register #(.width(32)) _19 (.D(i19), .Q(o19), .clk(clk), .clr(reset));  // open: en
  Register #(.width(32)) _20 (.D(i20), .Q(o20), .clk(clk), .clr(reset));  // open: en
  Register #(.width(32)) _21 (.D(i21), .Q(o21), .clk(clk), .clr(reset));  // open: en
  Register #(.width(32)) _22 (.D(i22), .Q(o22), .clk(clk), .clr(reset));  // open: en
  Register #(.width(32)) _23 (.D(i23), .Q(o23), .clk(clk), .clr(reset));  // open: en
  Register #(.width(32)) _24 (.D(i24), .Q(o24), .clk(clk), .clr(reset));  // open: en
  Register #(.width(32)) _25 (.D(i25), .Q(o25), .clk(clk), .clr(reset));  // open: en
  Register #(.width(32)) _26 (.D(i26), .Q(o26), .clk(clk), .clr(reset));  // open: en
  Register #(.width(32)) _27 (.D(i27), .Q(o27), .clk(clk), .clr(reset));  // open: en
  Register #(.width(32)) _28 (.D(i28), .Q(o28), .clk(clk), .clr(reset));  // open: en
  Register #(.width(32)) _29 (.D(i29), .Q(o29), .clk(clk), .clr(reset));  // open: en
  Register #(.width(32)) _30 (.D(i30), .en(undriven), .Q(o30), .clk(clk), .clr(reset));
  Register #(.width(32)) _31 (.D(i31), .Q(o31), .clk(clk), .clr(reset));  // open: en
  Multiplexer #(.select(5), .width(32), .enable("false")) multiplexer_1 (
    .in0(o0), .in1(o1), .in2(o2), .in3(o3), .in4(o4), .in5(o5), .in6(o6), .in7(o7), .in8(o8), .in9(o9),
    .in10(o10), .in11(o11), .in12(o12), .in13(o13), .in14(o14), .in15(o15), .in16(o16), .in17(o17),
    .in18(o18), .in19(o19), .in20(o20), .in21(o21), .in22(o22), .in23(o23), .in24(o24), .in25(o25),
    .in26(o26), .in27(o27), .in28(o28), .in29(o29), .in30(o30), .in31(o31), .out(RD1), .sel(A1));
  Multiplexer #(.select(5), .width(32), .enable("false")) multiplexer_2 (
    .in0(o0), .in1(o1), .in2(o2), .in3(o3), .in4(o4), .in5(o5), .in6(o6), .in7(o7), .in8(o8), .in9(o9),
    .in10(o10), .in11(o11), .in12(o12), .in13(o13), .in14(o14), .in15(o15), .in16(o16), .in17(o17),
    .in18(o18), .in19(o19), .in20(o20), .in21(o21), .in22(o22), .in23(o23), .in24(o24), .in25(o25),
    .in26(o26), .in27(o27), .in28(o28), .in29(o29), .in30(o30), .in31(o31), .out(RD2), .sel(A2));
endmodule

module Controller (
  input  [5:0] opcode,
  input  [5:0] funct,
  output MemtoReg,
  output MemWrite,
  output Branch,
  output ALUSrc,
  output RegDst,
  output RegWrite,
  output [1:0] EXTop,
  output [2:0] ALUop,
  output isJ,
  output isLHU
);

  wire addu, andi, beq, jal, lhu, lui, lw, nf0, nf1, nf2, nf3, nf4, nf5, no0, no1, no2, no3, no4, no5, ori,
       subu, sw;

  not not_1 (no5, opcode[5]);
  not not_2 (no0, opcode[0]);
  not not_3 (no1, opcode[1]);
  not not_4 (no2, opcode[2]);
  not not_5 (no3, opcode[3]);
  not not_6 (no4, opcode[4]);
  not not_7 (nf0, funct[0]);
  not not_8 (nf5, funct[5]);
  not not_9 (nf1, funct[1]);
  not not_10 (nf4, funct[4]);
  not not_11 (nf2, funct[2]);
  not not_12 (nf3, funct[3]);
  and u_addu (addu, no5, no4, no3, no2, no1, no0, funct[5], nf4, nf3, nf2, nf1, funct[0]);
  and u_subu (subu, no5, no4, no3, no2, no1, no0, funct[5], nf4, nf3, nf2, funct[1], funct[0]);
  and u_ori (ori, no5, no4, opcode[3], opcode[2], no1, opcode[0]);
  and u_andi (andi, no5, no4, opcode[3], opcode[2], no1, no0);
  and u_lw (lw, opcode[5], no4, no3, no2, opcode[1], opcode[0]);
  and u_sw (sw, opcode[5], no4, opcode[3], no2, opcode[1], opcode[0]);
  and u_beq (beq, no5, no4, no3, opcode[2], no1, no0);
  and u_lui (lui, no5, no4, opcode[3], opcode[2], opcode[1], opcode[0]);
  and u_jal (jal, no5, no4, no3, no2, opcode[1], opcode[0]);
  and u_lhu (lhu, opcode[5], no4, no3, opcode[2], no1, opcode[0]);
  or or_1 (EXTop[0], lw, sw, beq, lhu);
  buf or_2 (EXTop[1], lui);  // OR_Gate
  or or_3 (MemtoReg, lw, lhu);
  buf or_4 (MemWrite, sw);  // OR_Gate
  buf or_5 (Branch, beq);  // OR_Gate
  or or_6 (ALUSrc, lw, sw, ori, andi, lui, lhu);
  or or_7 (RegDst, addu, subu);
  or or_8 (RegWrite, addu, subu, ori, andi, lw, lui, jal, lhu);
  or beq_sub (ALUop[0], subu, andi, beq);
  or or_9 (ALUop[1], andi, ori);
  buf or_10 (isJ, jal);  // OR_Gate
  buf or_11 (isLHU, lhu);  // OR_Gate

  assign ALUop[2] = 1'b0;

  // Other names for the same wires on the sheet: f0 = funct[0]; f1 = funct[1]; f2 = funct[2]; f3 = funct[3];
  //   f4 = funct[4]; f5 = funct[5]; o0 = opcode[0]; o1 = opcode[1]; o2 = opcode[2]; o3 = opcode[3]; o4 = opcode[4];
  //   o5 = opcode[5]
endmodule

module IFU (
  input  CLK,
  input  Reset,
  input  Branch,
  input  [31:0] Zero,
  input  isJ,
  output [31:0] Instr,
  output [31:0] PC_4
);

  wire and_1_out, not_1_out, or_1_out;
  wire [3:0] _31_28;
  wire [27:0] register_1_q;
  wire [31:0] adder_2_out, bit_extender_1_out, notJ, nPC;

  or or_1 (or_1_out, Zero[15], Zero[0], Zero[1], Zero[2], Zero[3], Zero[4], Zero[5], Zero[6], Zero[7], Zero[8], Zero[9], Zero[10], Zero[11], Zero[12], Zero[13], Zero[14], Zero[16], Zero[17], Zero[18], Zero[19], Zero[20], Zero[21], Zero[22], Zero[23], Zero[24], Zero[25], Zero[26], Zero[27], Zero[28], Zero[29], Zero[30], Zero[31]);
  not not_1 (not_1_out, or_1_out);
  and and_1 (and_1_out, not_1_out, Branch);
  Multiplexer #(.width(32)) multiplexer_1 (.in0(PC_4), .in1(adder_2_out), .out(notJ), .sel(and_1_out));  // open: en
  Register #(.width(32)) register_1 (.D(nPC), .Q({_31_28, register_1_q}), .clk(CLK), .clr(Reset));  // open: en
  Multiplexer #(.width(32)) multiplexer_2 (
    .in0(notJ), .in1({_31_28, Instr[25:0], 2'b00}), .out(nPC), .sel(isJ));  // open: en
  assign bit_extender_1_out = {{16{Instr[15]}}, Instr[15:0]};  // Bit_Extender bit_extender_1
  Adder #(.width(32)) adder_1 (.a(32'h4), .b({_31_28, register_1_q}), .out(PC_4));  // open: cin, cout
  Adder #(.width(32)) adder_2 (.a({bit_extender_1_out[29:0], 2'b00}), .b(PC_4), .out(adder_2_out));  // open: cin, cout
  ROM #(.addrWidth(5), .dataWidth(32)) rom_1 (.addr(register_1_q[6:2]), .data(Instr));  // open: sel

  // Other names for the same wires on the sheet: instr_index[25:0] = Instr[25:0]; offset[15:0] = Instr[15:0]
endmodule
