// Logisim project fsm-one_gate.circ as structural Verilog: 2 circuits, main circuit fsm
module fsm (
  input  in_1,
  input  [1:0] in_2,
  output out_3
);

  wire clock_1_out, clr, not_1_out;
  wire [1:0] judge_1_o0, register_2_q;

  Register #(.width(1)) register_1 (.D(in_1), .Q(clr), .clk(clock_1_out), .clr(not_1_out));  // open: en
  not not_1 (not_1_out, in_1);
  judge judge_1 (
    .R1(register_2_q[1]), .R0(register_2_q[0]), .I1(in_2[1]), .I0(in_2[0]), .O1(judge_1_o0[1]),
    .O0(judge_1_o0[0]), .Out(out_3));
  Clock clock_1 (.out(clock_1_out));
  Register #(.width(2)) register_2 (.D(judge_1_o0), .Q(register_2_q), .clk(clock_1_out), .clr(clr));  // open: en
endmodule

module judge (
  input  R1,
  input  R0,
  input  I1,
  input  I0,
  output O1,
  output O0,
  output Out
);

  wire not_1_out, not_2_out, not_3_out, not_4_out, not_5_out;

  not not_1 (not_1_out, R1);
  and and_1 (O1, not_1_out, R0, not_2_out);
  not not_2 (not_2_out, I0);
  not not_3 (not_3_out, I1);
  and and_2 (O0, not_3_out, I0);
  not not_4 (not_4_out, R0);
  and and_3 (Out, R1, not_4_out, not_5_out);
  not not_5 (not_5_out, I0);
endmodule
