// Logisim project mod5.circ as structural Verilog: 2 circuits, main circuit mod5
module mod5 (
  input  in_1,
  output out_2,
  output out_3,
  output out_4,
  output out_5,
  output out_6
);

  wire clock_1_out, register_1_q;

  Register #(.width(1)) register_1 (.D(in_1), .Q(register_1_q), .clk(clock_1_out));  // open: en, clr
  Clock clock_1 (.out(clock_1_out));
  fck fck_1 (.s(register_1_q), .i(in_1), .r0(out_2), .r1(out_3), .r2(out_4), .r3(out_5), .r4(out_6));
endmodule

module fck (
  input  s,
  input  i,
  output r0,
  output r1,
  output r2,
  output r3,
  output r4
);

  wire not_1_out, not_2_out, not_3_out, not_4_out;

  not not_1 (not_1_out, s);
  not not_2 (not_2_out, i);
  not not_3 (not_3_out, s);
  and and_1 (r3, s, i);
  not not_4 (not_4_out, i);
  and and_2 (r1, not_1_out, not_2_out);
  and and_3 (r2, not_3_out, i);
  and and_4 (r4, s, not_4_out);

  assign r0 = 1'b0;
endmodule
