// Logisim project swap.circ as structural Verilog
module swap (
  input  I1,
  input  I2,
  input  S,
  output O1,
  output O2
);

  wire and_1_out, and_2_out, and_3_out, and_4_out, not_1_out;

  not not_1 (not_1_out, S);
  and and_1 (and_1_out, not_1_out, I1);
  and and_2 (and_2_out, S, I2);
  and and_3 (and_3_out, S, I1);
  and and_4 (and_4_out, I2, not_1_out);
  or or_1 (O1, and_1_out, and_2_out);
  or or_2 (O2, and_3_out, and_4_out);
endmodule

module test (
  input  A,
  input  B,
  input  C,
  output Y
);

  wire and_1_out, and_2_out, and_3_out;

  and and_1 (and_1_out, A, B);
  and and_2 (and_2_out, B, C);
  and and_3 (and_3_out, C, A);
  or or_1 (Y, and_1_out, and_2_out, and_3_out);
endmodule

module half_adder (
  input  a1,
  input  a0,
  input  b1,
  input  b0,
  output c,
  output s1,
  output s0
);

  wire and_1_out, and_2_out, and_3_out, and_4_out, and_5_out, and_6_out, and_7_out, and_8_out, and_9_out,
       and_10_out, and_11_out, not_1_out, not_2_out, not_3_out, not_4_out, not_5_out, not_6_out, not_7_out,
       not_8_out, not_9_out, not_10_out, not_11_out, not_12_out;

  and and_1 (and_1_out, a0, b1, b0);
  and and_2 (and_2_out, a1, b1);
  and and_3 (and_3_out, a1, a0, b0);
  not not_1 (not_1_out, a1);
  not not_2 (not_2_out, a0);
  not not_3 (not_3_out, a1);
  not not_4 (not_4_out, b0);
  not not_5 (not_5_out, a1);
  not not_6 (not_6_out, b1);
  not not_7 (not_7_out, a0);
  not not_8 (not_8_out, b1);
  not not_9 (not_9_out, b1);
  not not_10 (not_10_out, b0);
  not not_11 (not_11_out, a0);
  and and_4 (and_4_out, not_11_out, b0);
  and and_5 (and_5_out, a0, not_12_out);
  not not_12 (not_12_out, b0);
  or or_1 (c, and_1_out, and_2_out, and_3_out);
  and and_6 (and_6_out, not_1_out, not_2_out, b1);
  and and_7 (and_7_out, not_3_out, b1, not_4_out);
  and and_8 (and_8_out, not_5_out, a0, not_6_out, b0);
  and and_9 (and_9_out, a1, not_7_out, not_8_out);
  and and_10 (and_10_out, a1, not_9_out, not_10_out);
  and and_11 (and_11_out, a1, a0, b1, b0);
  or or_2 (s0, and_4_out, and_5_out);
  or or_3 (s1, and_6_out, and_7_out, and_8_out, and_9_out, and_10_out, and_11_out);
endmodule

module full_adder (
  input  a0,
  input  a1,
  input  b0,
  input  b1,
  input  c0,
  output c1,
  output s0,
  output s1
);

  wire and_1_out, and_2_out, and_3_out, and_4_out, and_5_out, and_6_out, and_7_out, and_8_out, and_9_out,
       and_10_out, and_11_out, and_12_out, and_13_out, and_14_out, and_15_out, and_16_out, and_17_out,
       and_18_out, and_19_out, and_20_out, and_21_out, and_22_out, not_1_out, not_2_out, not_3_out,
       not_4_out, not_5_out, not_6_out, not_7_out, not_8_out, not_9_out, not_10_out, not_11_out, not_12_out,
       not_13_out, not_14_out, not_15_out, not_16_out, not_17_out, not_18_out, not_19_out, not_20_out,
       not_21_out, not_22_out, not_23_out, not_24_out, not_25_out;

  not not_1 (not_1_out, a1);
  not not_2 (not_2_out, b0);
  not not_3 (not_3_out, a0);
  not not_4 (not_4_out, a1);
  not not_5 (not_5_out, b1);
  not not_6 (not_6_out, a0);
  not not_7 (not_7_out, a1);
  not not_8 (not_8_out, c0);
  not not_9 (not_9_out, a0);
  not not_10 (not_10_out, b1);
  not not_11 (not_11_out, c0);
  not not_12 (not_12_out, a0);
  not not_13 (not_13_out, b0);
  not not_14 (not_14_out, a0);
  not not_15 (not_15_out, b0);
  not not_16 (not_16_out, b0);
  not not_17 (not_17_out, b1);
  not not_18 (not_18_out, c0);
  not not_19 (not_19_out, a1);
  not not_20 (not_20_out, b1);
  not not_21 (not_21_out, a1);
  not not_22 (not_22_out, c0);
  not not_23 (not_23_out, b1);
  not not_24 (not_24_out, c0);
  not not_25 (not_25_out, a0);
  and and_1 (and_1_out, b0, b1, c0);
  and and_2 (and_2_out, a1, b0, c0);
  and and_3 (and_3_out, a1, b0, b1);
  and and_4 (and_4_out, a0, not_1_out);
  and and_5 (and_5_out, a0, c0);
  and and_6 (and_6_out, a0, b1);
  and and_7 (and_7_out, a0, b0);
  and and_8 (and_8_out, not_2_out, b1, c0);
  and and_9 (and_9_out, not_3_out, not_4_out, b0, not_5_out);
  and and_10 (and_10_out, not_6_out, not_7_out, b0, not_8_out);
  and and_11 (and_11_out, not_9_out, b0, not_10_out, not_11_out);
  and and_12 (and_12_out, not_12_out, a1, not_13_out, c0);
  and and_13 (and_13_out, not_14_out, a1, not_15_out, b1);
  and and_14 (and_14_out, a0, b1, c0);
  and and_15 (and_15_out, a0, a1, not_16_out, not_17_out, not_18_out);
  and and_16 (and_16_out, a0, a1, b0, c0);
  and and_17 (and_17_out, a0, a1, b0, b1);
  and and_18 (and_18_out, not_19_out, not_20_out, c0);
  and and_19 (and_19_out, not_21_out, b1, not_22_out);
  and and_20 (and_20_out, a1, not_23_out, not_24_out);
  and and_21 (and_21_out, not_25_out, a1, b1, c0);
  and and_22 (and_22_out, a1, b0, b1, c0);
  or or_1 (c1, and_1_out, and_2_out, and_3_out, and_4_out, and_5_out, and_6_out, and_7_out);
  or or_2 (s0, and_8_out, and_9_out, and_10_out, and_11_out, and_12_out, and_13_out, and_14_out, and_15_out, and_16_out, and_17_out);
  or or_3 (s1, and_18_out, and_19_out, and_20_out, and_21_out, and_22_out);
endmodule

module _1bit_swap (
  input  A,
  input  B,
  input  C,
  output O1,
  output O2
);

  wire and_1_out, and_2_out, and_3_out, and_4_out, not_1_out, not_2_out;

  not not_1 (not_1_out, C);
  not not_2 (not_2_out, C);
  and and_1 (and_1_out, B, C);
  and and_2 (and_2_out, A, not_1_out);
  and and_3 (and_3_out, B, not_2_out);
  and and_4 (and_4_out, A, C);
  or or_1 (O1, and_1_out, and_2_out);
  or or_2 (O2, and_3_out, and_4_out);
endmodule
