// Logisim project 售货机.circ as structural Verilog: 4 circuits, main circuit main
module main (
  input  [1:0] in,
  input  reset,
  output \output ,
  output rd4,
  output rd2,
  output rd1
);

  wire back, clock_1_out, not_1_out, not_2_out, not_3_out, zero;
  wire [3:0] adder_1_out, \input , multiplexer_1_out, register_1_q;

  reroll reroll_1 (.In1(in[1]), .In0(in[0]), .Ou3(\input [3]), .Ou2(\input [2]), .Ou1(\input [1]), .Ou0(\input [0]));
  or or_1 (zero, reset, back);
  not not_1 (not_1_out, \output );
  Multiplexer #(.width(4), .enable("false")) multiplexer_1 (
    .in0(4'b0000), .in1(register_1_q), .out(multiplexer_1_out), .sel(not_1_out));
  Adder #(.width(4)) adder_1 (.a(multiplexer_1_out), .b(\input ), .out(adder_1_out));  // open: cin, cout
  Register #(.width(4)) register_1 (.D(adder_1_out), .Q(register_1_q), .clk(clock_1_out), .clr(zero));  // open: en
  Clock clock_1 (.out(clock_1_out));
  not not_2 (not_2_out, clock_1_out);
  putout putout_1 (
    .i3(register_1_q[3]), .i2(register_1_q[2]), .i1(register_1_q[1]), .i0(register_1_q[0]), .out(\output ),
    .r4(rd4), .r2(rd2), .r1(rd1));
  not not_3 (not_3_out, \output );
  Register #(.width(1)) register_2 (.D(\output ), .Q(back), .clk(not_2_out), .clr(not_3_out));  // open: en
endmodule

module reroll (
  input  In1,
  input  In0,
  output Ou3,
  output Ou2,
  output Ou1,
  output Ou0
);

  wire not_1_out;

  and and_1 (Ou2, In1, In0);
  not not_1 (not_1_out, In0);
  and and_2 (Ou1, In1, not_1_out);

  assign Ou0 = In0;
  assign Ou3 = 1'b0;
endmodule

module putout (
  input  i3,
  input  i2,
  input  i1,
  input  i0,
  output out,
  output r4,
  output r2,
  output r1
);

  wire and_1_out, and_2_out, and_4_out, and_5_out, and_6_out, and_7_out, not_1_out, not_2_out, not_3_out;

  and and_1 (and_1_out, i2, i0);
  and and_2 (and_2_out, i2, i1);
  and and_3 (r4, i3, i0);
  and and_4 (and_4_out, i2, i1, i0);
  and and_5 (and_5_out, i3, not_1_out);
  not not_1 (not_1_out, i0);
  and and_6 (and_6_out, i2, i1, not_2_out);
  not not_2 (not_2_out, i0);
  and and_7 (and_7_out, i3, not_3_out);
  not not_3 (not_3_out, i0);
  or or_1 (out, and_1_out, and_2_out, i3);
  or or_2 (r2, and_4_out, and_5_out);
  or or_3 (r1, and_6_out, and_7_out);
endmodule

module move (
  input  [7:0] in_1,
  input  [2:0] in_2,
  output [7:0] out_3
);

  wire [7:0] multiplexer_1_out, multiplexer_2_out;

  Multiplexer #(.width(8), .enable("false")) multiplexer_1 (
    .in0(in_1), .in1({{2{in_1[7]}}, in_1[6:1]}), .out(multiplexer_1_out), .sel(in_2[0]));
  Multiplexer #(.width(8), .enable("false")) multiplexer_2 (
    .in0(multiplexer_1_out), .in1({{3{in_1[7]}}, multiplexer_1_out[6:2]}), .out(multiplexer_2_out),
    .sel(in_2[1]));
  Multiplexer #(.width(8), .enable("false")) multiplexer_3 (
    .in0(multiplexer_2_out), .in1({{5{in_1[7]}}, multiplexer_2_out[6:4]}), .out(out_3), .sel(in_2[2]));

  // Other names for the same wires on the sheet: _7 = in_1[7]
endmodule
