// Logisim project 屌丝售货机.circ as structural Verilog: 3 circuits, main circuit main
module main (
  input  [1:0] In,
  input  clr,
  output Output,
  output Rest
);

  wire back, clock_1_out, not_1_out, not_2_out, zero;
  wire [2:0] adder_1_out, multiplexer_1_out, register_1_q, transfer_1_o0;

  transfer transfer_1 (.I1(In[1]), .I0(In[0]), .O2(transfer_1_o0[2]), .O1(transfer_1_o0[1]), .O0(transfer_1_o0[0]));
  or or_1 (zero, clr, back);
  Multiplexer #(.width(3), .enable("false")) multiplexer_1 (
    .in0(register_1_q), .in1(3'b000), .out(multiplexer_1_out), .sel(Output));
  Adder #(.width(3)) adder_1 (.a(transfer_1_o0), .b(multiplexer_1_out), .out(adder_1_out));  // open: cin, cout
  Clock clock_1 (.out(clock_1_out));
  Register #(.width(3)) register_1 (.D(adder_1_out), .Q(register_1_q), .clk(clock_1_out), .clr(zero));  // open: en
  not not_1 (not_1_out, clock_1_out);
  Output output_1 (.I2(register_1_q[2]), .I1(register_1_q[1]), .I0(register_1_q[0]), .O(Output), .R(Rest));
  Register #(.width(1)) register_2 (.D(Output), .Q(back), .clk(not_1_out), .clr(not_2_out));  // open: en
  not not_2 (not_2_out, Output);
endmodule

module transfer (
  input  I1,
  input  I0,
  output O2,
  output O1,
  output O0
);


  assign O0 = I0;
  assign O1 = I1;
  assign O2 = 1'b0;
endmodule

module Output (
  input  I2,
  input  I1,
  input  I0,
  output O,
  output R
);

  and and_1 (R, I2, I0);

  assign O = I2;
endmodule
