// Logisim project 抢答.circ as structural Verilog: 1 circuit, main circuit main
module main (
  input  in_1,
  input  A,
  input  B,
  input  C,
  input  D
);

  wire a_t, b_t, c_t, clk, clock_1_out, d_t, register_1_q, register_2_q, register_3_q, register_4_q;

  Register #(.width(1)) register_1 (.D(A), .Q(register_1_q), .clk(clk), .clr(in_1));  // open: en
  Register #(.width(1)) register_2 (.D(B), .Q(register_2_q), .clk(clk), .clr(in_1));  // open: en
  Register #(.width(1)) register_3 (.D(C), .Q(register_3_q), .clk(clk), .clr(in_1));  // open: en
  Register #(.width(1)) register_4 (.D(D), .Q(register_4_q), .clk(clk), .clr(in_1));  // open: en
  not not_1 (a_t, register_1_q);
  not not_2 (b_t, register_2_q);
  not not_3 (c_t, register_3_q);
  not not_4 (d_t, register_4_q);
  LED led_1 (.in(register_1_q));
  LED led_2 (.in(register_2_q));
  LED led_3 (.in(register_3_q));
  LED led_4 (.in(register_4_q));
  Clock clock_1 (.out(clock_1_out));
  nand nand_1 (clk, a_t, b_t, c_t, d_t, clock_1_out);

  // Other names for the same wires on the sheet: reset = in_1
endmodule
