// Logisim project 苦逼售货机.circ as structural Verilog: 3 circuits, main circuit main
module main (
  input  in_1,
  output out_2,
  output out_3
);

  wire clock_1_out, not_1_out, register_2_q;
  wire [2:0] register_1_q, std_1_o0;

  std std_1 (
    .i2(register_1_q[2]), .i1(register_1_q[1]), .i0(register_1_q[0]), .i(in_1), .o2(std_1_o0[2]),
    .o1(std_1_o0[1]), .o0(std_1_o0[0]));
  Register #(.width(3)) register_1 (.D(std_1_o0), .Q(register_1_q), .clk(clock_1_out), .clr(register_2_q));  // open: en
  Clock clock_1 (.out(clock_1_out));
  opt opt_1 (.i2(register_1_q[2]), .i1(register_1_q[1]), .i0(register_1_q[0]), .o(out_2), .r(out_3));
  Register #(.width(1)) register_2 (.D(out_2), .Q(register_2_q), .clk(clock_1_out), .clr(not_1_out));  // open: en
  not not_1 (not_1_out, out_2);
endmodule

module std (
  input  i2,
  input  i1,
  input  i0,
  input  i,
  output o2,
  output o1,
  output o0
);

  wire and_1_out, and_2_out, and_3_out, and_4_out, and_5_out, and_6_out, and_7_out, not_1_out, not_2_out,
       not_3_out, not_4_out, not_5_out, not_6_out, not_7_out, not_8_out, not_9_out, not_10_out, not_11_out,
       not_12_out, not_13_out, not_14_out;

  not not_1 (not_1_out, i2);
  and and_1 (and_1_out, not_1_out, i1, i);
  not not_2 (not_2_out, i2);
  and and_2 (and_2_out, not_2_out, i1, i0);
  not not_3 (not_3_out, i2);
  not not_4 (not_4_out, i1);
  not not_5 (not_5_out, i2);
  not not_6 (not_6_out, i0);
  not not_7 (not_7_out, i);
  not not_8 (not_8_out, i2);
  not not_9 (not_9_out, i1);
  and and_3 (and_3_out, not_8_out, not_9_out, not_10_out);
  not not_10 (not_10_out, i0);
  not not_11 (not_11_out, i2);
  not not_12 (not_12_out, i0);
  and and_4 (and_4_out, not_11_out, not_12_out, not_13_out);
  not not_13 (not_13_out, i);
  not not_14 (not_14_out, i2);
  and and_5 (and_5_out, not_14_out, i0, i);
  or or_1 (o2, and_1_out, and_2_out);
  and and_6 (and_6_out, not_3_out, not_4_out, i0);
  or or_2 (o1, and_6_out, and_7_out);
  and and_7 (and_7_out, not_5_out, i1, not_6_out, not_7_out);
  or or_3 (o0, and_3_out, and_4_out, and_5_out);
endmodule

module opt (
  input  i2,
  input  i1,
  input  i0,
  output o,
  output r
);

  wire not_1_out, not_2_out;

  not not_1 (not_1_out, i1);
  not not_2 (not_2_out, i1);
  and and_1 (o, i2, not_1_out);
  and and_2 (r, i2, not_2_out, i0);
endmodule
